// Logisim project 1x8 Demux.circ as structural Verilog: 1 circuit, main circuit main
module main (
  input  C,
  input  B,
  input  A,
  input  IN,
  input  IN_2,
  input  [2:0] C_B_A,
  output I0,
  output I0_2,
  output I1,
  output I1_2,
  output I2,
  output I2_2,
  output I3,
  output I4,
  output I3_2,
  output I5,
  output I6,
  output I4_2,
  output I7,
  output I5_2,
  output I6_2,
  output I7_2
);

  wire not_1_out, not_2_out, not_3_out;

  not not_1 (not_1_out, C);
  not not_2 (not_2_out, B);
  not not_3 (not_3_out, A);
  and and_1 (I0, IN, not_3_out, not_2_out, not_1_out);
  and and_2 (I1, IN, A, not_2_out, not_1_out);
  and and_3 (I2_2, IN, not_3_out, B, not_1_out);
  and and_4 (I3_2, IN, A, B, not_1_out);
  and and_5 (I4_2, IN, not_3_out, not_2_out, C);
  and and_6 (I5_2, IN, A, not_2_out, C);
  and and_7 (I6_2, IN, not_3_out, B, C);
  and and_8 (I7_2, IN, A, B, C);
  Demultiplexer #(.select(3)) demultiplexer_1 (
    .out0(I0_2), .out1(I1_2), .out2(I2), .out3(I3), .out4(I4), .out5(I5), .out6(I6), .out7(I7), .in(IN_2),
    .sel(C_B_A));  // open: en

  // Notes on the sheet:
  //   1X8 DEMUX
endmodule
