// Logisim project 4x1 mux.circ as structural Verilog: 1 circuit, main circuit main
module main (
  input  S1,
  input  S0,
  input  I0,
  input  I0_2,
  input  I1,
  input  I2,
  input  I3,
  input  I1_2,
  input  [1:0] S1_S0,
  input  I2_2,
  input  I3_2,
  output out_12,
  output out_13
);

  wire and_1_out, and_2_out, and_3_out, and_4_out, not_1_out, not_2_out;

  not not_1 (not_1_out, S1);
  not not_2 (not_2_out, S0);
  and and_1 (and_1_out, not_2_out, not_1_out, I0_2);
  and and_2 (and_2_out, S0, not_1_out, I1_2);
  and and_3 (and_3_out, not_2_out, S1, I2_2);
  and and_4 (and_4_out, S0, S1, I3_2);
  or or_1 (out_13, and_1_out, and_2_out, and_3_out, and_4_out);
  Multiplexer #(.select(2)) multiplexer_1 (
    .in0(I0), .in1(I1), .in2(I2), .in3(I3), .out(out_12), .sel(S1_S0));  // open: en

  // Notes on the sheet:
  //   4X1 MUX
endmodule
