// Logisim project 4x1 with 2x1 mux.circ as structural Verilog: 1 circuit, main circuit main
module main (
  input  S0,
  input  S1,
  input  I0,
  input  I0_2,
  input  I1,
  input  I1_2,
  input  S0_2,
  input  I2,
  input  I3,
  input  I2_2,
  input  S1_2,
  input  I3_2,
  output out_13,
  output out_14
);

  wire and_1_out, and_2_out, and_3_out, and_4_out, and_5_out, and_6_out, multiplexer_1_out,
       multiplexer_2_out, not_1_out, not_2_out, or_1_out, or_2_out;

  not not_1 (not_1_out, S0);
  and and_1 (and_1_out, not_1_out, I0);
  or or_1 (or_1_out, and_1_out, and_2_out);
  and and_2 (and_2_out, S0, I1_2);
  and and_3 (and_3_out, not_1_out, I2_2);
  or or_2 (or_2_out, and_3_out, and_4_out);
  and and_4 (and_4_out, S0, I3_2);
  not not_2 (not_2_out, S1);
  and and_5 (and_5_out, not_2_out, or_1_out);
  and and_6 (and_6_out, S1, or_2_out);
  or or_3 (out_14, and_5_out, and_6_out);
  Multiplexer multiplexer_1 (.in0(I0_2), .in1(I1), .out(multiplexer_1_out), .sel(S0_2));  // open: en
  Multiplexer multiplexer_2 (.in0(I2), .in1(I3), .out(multiplexer_2_out), .sel(S0_2));  // open: en
  Multiplexer multiplexer_3 (.in0(multiplexer_1_out), .in1(multiplexer_2_out), .out(out_13), .sel(S1_2));  // open: en

  // Notes on the sheet:
  //   4X1 MUX USING 2X1 MUX
endmodule
