// Logisim project W1.circ as structural Verilog: 1 circuit, main circuit main
module main (
  input  X,
  input  Y,
  input  Z,
  output W
);

  wire nand_1_out, nand_2_out, nand_3_out, nand_4_out, nand_5_out, nand_6_out, nand_7_out, nand_8_out,
       nand_9_out, nand_10_out, nand_11_out;

  nand nand_1 (nand_1_out, Y, Y);
  nand nand_2 (nand_2_out, X, X);
  nand nand_3 (nand_3_out, nand_1_out, nand_1_out);
  nand nand_4 (nand_4_out, Z, Z);
  nand nand_5 (nand_5_out, nand_2_out, Y);
  nand nand_6 (nand_6_out, nand_3_out, nand_4_out);
  nand nand_7 (nand_7_out, nand_5_out, nand_5_out);
  nand nand_8 (nand_8_out, X, nand_6_out);
  nand nand_9 (nand_9_out, nand_8_out, nand_8_out);
  nand nand_10 (nand_10_out, nand_7_out, nand_7_out);
  nand nand_11 (nand_11_out, nand_9_out, nand_9_out);
  nand nand_12 (W, nand_11_out, nand_10_out);

  // Notes on the sheet:
  //   Y'
  //   X'
  //   W=X(Y'+Z)+X'Y
  //   Y'+Z
  //   X'Y
  //   X(Y'+Z)
endmodule
