// Logisim project W2.circ as structural Verilog: 1 circuit, main circuit main
module main (
  input  A,
  input  B,
  input  C,
  output W
);

  wire nor_1_out, nor_2_out, nor_3_out, nor_4_out, nor_5_out, nor_6_out, nor_7_out;

  nor nor_1 (nor_1_out, A, A);
  nor nor_2 (nor_2_out, B, B);
  nor nor_3 (nor_3_out, C, C);
  nor nor_4 (nor_4_out, nor_1_out, nor_2_out);
  nor nor_5 (nor_5_out, nor_1_out, nor_3_out);
  nor nor_6 (nor_6_out, nor_2_out, C);
  nor nor_7 (nor_7_out, nor_4_out, nor_5_out, nor_6_out);
  nor nor_8 (W, nor_7_out, nor_7_out);

  // Notes on the sheet:
  //   A'
  //   B'
  //   C'
  //   W=AB'C+A'BC'+AB
  //   =AB+AC+BC'
  //   AB
  //   AC
  //   BC'
endmodule
