// Logisim project and.circ as structural Verilog: 1 circuit, main circuit main
module main (
  input  A,
  input  B,
  input  A_2,
  input  B_2,
  input  A_3,
  input  B_3,
  input  A_4,
  input  B_4,
  output AB,
  output AB_2,
  output AB_3,
  output AB_4
);

  and and_1 (AB, A, B);
  and and_2 (AB_2, A_2, B_2);
  and and_3 (AB_3, A_3, B_3);
  and and_4 (AB_4, A_4, B_4);

  // Notes on the sheet:
  //   AND
endmodule
