// Logisim project decimal to bcd encoder.circ as structural Verilog: 2 circuits, main circuit main
module main (
  input  I0,
  input  I1,
  input  I0_2,
  input  I1_2,
  input  I2,
  input  I2_2,
  input  I3,
  input  I3_2,
  input  I4,
  input  I4_2,
  input  I5,
  input  I6,
  input  I5_2,
  input  I7,
  input  I8,
  input  I6_2,
  input  I9,
  input  I7_2,
  input  I8_2,
  input  I9_2,
  output A,
  output B,
  output A_2,
  output B_2,
  output C,
  output D,
  output C_2,
  output D_2
);

  or or_1 (A, I1, I3_2, I5_2, I7_2, I9_2);
  or or_2 (B, I2, I3_2, I6_2, I7_2);
  or or_3 (C_2, I4_2, I5_2, I6_2, I7_2);
  or or_4 (D_2, I8_2, I9_2);
  encoder encoder_1 (
    .I0(I0_2), .I1(I1_2), .I2(I2_2), .I3(I3), .I4(I4), .I5(I5), .I6(I6), .I7(I7), .I8(I8), .I9(I9), .A(A_2),
    .B(B_2), .C(C), .D(D));

  // Notes on the sheet:
  //   I1+I3+I5+I7+I9
  //   I2+I3+I6+I7
  //   I4+I5+I6+I7
  //   I8+I9
  //   DECIMAL TO BCD ENCODER
endmodule

module encoder (
  input  I0,
  input  I1,
  input  I2,
  input  I3,
  input  I4,
  input  I5,
  input  I6,
  input  I7,
  input  I8,
  input  I9,
  output A,
  output B,
  output C,
  output D
);

  or or_1 (A, I1, I3, I5, I7, I9);
  or or_2 (B, I2, I3, I6, I7);
  or or_3 (C, I4, I5, I6, I7);
  or or_4 (D, I8, I9);

  // Notes on the sheet:
  //   DECIMAL TO BCD ENCODER
  //   I1+I3+I5+I7+I9
  //   I2+I3+I6+I7
  //   I4+I5+I6+I7
  //   I8+I9
endmodule
