// Logisim project full subtractor.circ as structural Verilog: 1 circuit, main circuit main
module main (
  input  A,
  input  B,
  input  Bin,
  output D,
  output Bout
);

  wire and_1_out, and_2_out, not_1_out, not_2_out, xor_1_out;

  not not_1 (not_1_out, A);
  and and_1 (and_1_out, B, not_1_out);
  xor xor_1 (xor_1_out, A, B);
  not not_2 (not_2_out, xor_1_out);
  and and_2 (and_2_out, not_2_out, Bin);
  xor xor_2 (D, xor_1_out, Bin);
  or or_1 (Bout, and_1_out, and_2_out);

  // Notes on the sheet:
  //   FULL SUBTRACTOR
  //   A^B^Bin
  //   A'B+Bin(A^B)'
endmodule
