// Logisim project half adder.circ as structural Verilog: 1 circuit, main circuit main
module main (
  input  in_1,
  input  in_2,
  input  in_3,
  input  in_4,
  input  in_5,
  input  in_6,
  input  in_7,
  input  in_8,
  output SUM,
  output SUM_2,
  output CARRY,
  output CARRY_2,
  output SUM_3,
  output SUM_4,
  output CARRY_3,
  output CARRY_4
);

  xor xor_1 (SUM, in_1, in_3);
  and and_1 (CARRY, in_1, in_3);
  xor xor_2 (SUM_3, in_5, in_7);
  and and_2 (CARRY_3, in_5, in_7);
  xor xor_3 (SUM_2, in_2, in_4);
  and and_3 (CARRY_2, in_2, in_4);
  xor xor_4 (SUM_4, in_6, in_8);
  and and_4 (CARRY_4, in_6, in_8);

  // Notes on the sheet:
  //   HALF ADDER
endmodule
