// Logisim project half subtractor.circ as structural Verilog: 1 circuit, main circuit main
module main (
  input  A,
  input  B,
  output D,
  output Bout
);

  wire not_1_out;

  not not_1 (not_1_out, A);
  xor xor_1 (D, A, B);
  and and_1 (Bout, not_1_out, B);

  // Notes on the sheet:
  //   HALF SUBTRACTOR
  //   A^B
  //   A'B
endmodule
