// Logisim project nand.circ as structural Verilog: 1 circuit, main circuit main
module main (
  input  A,
  input  B,
  input  A_2,
  input  B_2,
  input  A_3,
  input  B_3,
  input  A_4,
  input  B_4,
  output C,
  output C_2,
  output C_3,
  output C_4
);

  nand nand_1 (C, A, B);
  nand nand_2 (C_2, A_2, B_2);
  nand nand_3 (C_3, A_3, B_3);
  nand nand_4 (C_4, A_4, B_4);

  // Notes on the sheet:
  //   NAND
endmodule
