// Logisim project nor.circ as structural Verilog: 1 circuit, main circuit main
module main (
  input  A,
  input  B,
  input  A_2,
  input  B_2,
  input  A_3,
  input  B_3,
  input  A_4,
  input  B_4,
  output A_B__prime,
  output A_B__prime_2,
  output A_B__prime_3,
  output A_B__prime_4
);

  nor nor_1 (A_B__prime, A, B);
  nor nor_2 (A_B__prime_2, A_2, B_2);
  nor nor_3 (A_B__prime_3, A_3, B_3);
  nor nor_4 (A_B__prime_4, A_4, B_4);

  // Notes on the sheet:
  //   NOR
endmodule
