// Logisim project not.circ as structural Verilog: 1 circuit, main circuit main
module main (
  input  X,
  input  X_2,
  output X_prime,
  output X_prime_2
);

  not not_1 (X_prime, X);
  not not_2 (X_prime_2, X_2);

  // Notes on the sheet:
  //   NOT
endmodule
