// Logisim project octal to binary encoder.circ as structural Verilog: 2 circuits, main circuit main
module main (
  input  I0,
  input  I0_2,
  input  I1,
  input  I1_2,
  input  I2,
  input  I2_2,
  input  I3,
  input  I3_2,
  input  I4,
  input  I5,
  input  I4_2,
  input  I6,
  input  I7,
  input  I5_2,
  input  I6_2,
  input  I7_2,
  output A,
  output A_2,
  output B,
  output B_2,
  output C,
  output C_2
);

  or or_1 (A, I1, I3_2, I5_2, I7_2);
  or or_2 (B, I2_2, I3_2, I6_2, I7_2);
  or or_3 (C_2, I4_2, I5_2, I6_2, I7_2);
  encoder encoder_1 (
    .I0(I0_2), .I1(I1_2), .I2(I2), .I3(I3), .I4(I4), .I5(I5), .I6(I6), .I7(I7), .A(A_2), .B(B_2), .C(C));

  // Notes on the sheet:
  //   I1+I3+I5+I7
  //   I2+I3+I6+I7
  //   I4+I5+I6+I7
  //   OCTAL TO BINARY ENCODER
endmodule

module encoder (
  input  I0,
  input  I1,
  input  I2,
  input  I3,
  input  I4,
  input  I5,
  input  I6,
  input  I7,
  output A,
  output B,
  output C
);

  or or_1 (A, I1, I3, I5, I7);
  or or_2 (B, I2, I3, I6, I7);
  or or_3 (C, I4, I5, I6, I7);

  // Notes on the sheet:
  //   I1+I3+I5+I7
  //   I2+I3+I6+I7
  //   I4+I5+I6+I7
  //   OCTAL TO BINARY ENCODER
endmodule
