// Logisim project or.circ as structural Verilog: 1 circuit, main circuit main
module main (
  input  A,
  input  B,
  input  A_2,
  input  B_2,
  input  A_3,
  input  B_3,
  input  A_4,
  input  B_4,
  output A_B,
  output A_B_2,
  output A_B_3,
  output A_B_4
);

  or or_1 (A_B, A, B);
  or or_2 (A_B_2, A_2, B_2);
  or or_3 (A_B_3, A_3, B_3);
  or or_4 (A_B_4, A_4, B_4);

  // Notes on the sheet:
  //   OR
endmodule
