// Logisim project xnor.circ as structural Verilog: 1 circuit, main circuit main
module main (
  input  in_1,
  input  in_2,
  input  in_3,
  input  in_4,
  input  in_5,
  input  in_6,
  input  in_7,
  input  in_8,
  output out_9,
  output out_10,
  output out_11,
  output out_12
);

  xnor xnor_1 (out_9, in_1, in_2);
  xnor xnor_2 (out_10, in_3, in_4);
  xnor xnor_3 (out_11, in_5, in_6);
  xnor xnor_4 (out_12, in_7, in_8);

  // Notes on the sheet:
  //   XNOR
endmodule
